# Fritzing sketch treat-dispenser (saved by Fritzing 0.9.3b)
breadboards: 1

parts:
  J1 = Basic Servo
  Part1 = Adafruit Feather M0 Bluefruit LE [part_number="Adafruit #2995"]

nets:
  GND: J1.gnd, Part1.GND
  N1: J1.vcc, Part1.VBUS
  N2: J1.pulse, Part1.A2

custom parts:
  Adafruit Feather M0 Bluefruit LE: This is the Adafruit Feather M0 Bluefruit LE - our take on an 'all-in-one' Arduino-compatible + Bluetooth Low Energy with built in USB and battery charging. Its an Adafruit Feather M0 with a BTLE module, ready to rock! We have other boards in the Feather family, check'em out here. Bluetooth Low Energy is the hottest new low-power, 2.4GHz spectrum wireless protocol. In particular, its the only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
